# Fritzing sketch Esquema elétrico estação meteorológica - v1 (saved by Fritzing 0.9.3b)
breadboards: 1

parts:
  DIP8 = attiny85 [package=dip]
  ESP8266 = WeMos D1 Mini
  Direção_do_Vento = Trimmer Potentiometer [maximum_resistance=80kΩ package=THT]
  Anemômetro = Reed switch [package=THT]
  Barômetro = Adafruit_BMP280
  Micro_SD = MicroSD Card Module
  SHT20 = Humidity Temperature Sensor SHT15
  R3 = Resistor [tolerance=±5% resistance=10k package=THT]
  R4 = Resistor [tolerance=±5% resistance=1k package=THT]
  R5 = Resistor [tolerance=±5% resistance=330 package=THT]
  D1 = Rectifier Diode [part_number=1N4001 package="Melf DO-213 AB [SMD]"]
  V1 = DC Power [voltage=5V]
  C4 = Ceramic Capacitor [capacitance=100nF package="100 mil [THT, multilayer]"]
  D2 = Rectifier Diode [part_number=1N4001 package="Melf DO-213 AB [SMD]"]
  R6 = Resistor [tolerance=±5% resistance=330 package=THT]
  R7 = Resistor [tolerance=±5% resistance=1k package=THT]
  C5 = Ceramic Capacitor [capacitance=100nF package="100 mil [THT, multilayer]"]
  Pluviômetro = Reed switch [package=THT]
  R10 = Resistor [tolerance=±5% resistance=220 package=THT]
  C6 = Ceramic Capacitor [capacitance=100nF package="100 mil [THT, multilayer]"]
  C7 = Ceramic Capacitor [capacitance=100nF package="100 mil [THT, multilayer]"]
  RTC1 = RTC Module
  D4 = Rectifier Diode [part_number=1N4001 package="Melf DO-213 AB [SMD]"]
  D5 = Rectifier Diode [part_number=1N4001 package="Melf DO-213 AB [SMD]"]
  R11 = Resistor [tolerance=±5% resistance=47k package=THT]
  C8 = Ceramic Capacitor [capacitance=100nF package="100 mil [THT, multilayer]"]
  C9 = Electrolytic Capacitor [capacitance=4.7mF package="100 mil [THT, electrolytic]"]
  C10 = Electrolytic Capacitor [capacitance=4.7mF package="100 mil [THT, electrolytic]"]
  S1 = Pushbutton [package=THT]

nets:
  N1: DIP8.Pin_2, Direção_do_Vento.leg2, R11.Pin_1
  N2: DIP8.Pin_3, ESP8266.D3
  GND: DIP8.Pin_4, ESP8266.G, Barômetro.GND, Micro_SD.GND, SHT20.GND, R3.Pin_0, V1.V-, D4.cathode, D5.cathode, C8.1, C9.-, C10.-
  N3: DIP8.Pin_5, ESP8266.RX
  N4: DIP8.Pin_6, C4.1, D2.cathode, R6.Pin_0
  N5: DIP8.Pin_7, R5.Pin_0, D1.cathode, C5.1
  VCC: DIP8.Pin_8, ESP8266.3V3, Barômetro.3.3V, Micro_SD.VCC, SHT20.VCC, R10.Pin_1, RTC1.VCC
  N6: ESP8266.5V, R11.Pin_0, C8.0, C9.+, S1.leg1
  N7: ESP8266.D0, ESP8266.RST
  N8: ESP8266.D1, Barômetro.SCK/SCL, SHT20.SCL, RTC1.SCL
  N9: ESP8266.D2, Barômetro.SDI/SDA, SHT20.SDA, RTC1.SDA
  N10: ESP8266.D5, Micro_SD.SCK
  N11: ESP8266.D6, Micro_SD.MISO, R10.Pin_0
  N12: ESP8266.D7, Micro_SD.MOSI
  N13: ESP8266.D8, Micro_SD.CS
  N14: Direção_do_Vento.wiper, R3.Pin_1
  N15: Anemômetro.pin_1, R4.Pin_1, R5.Pin_1, D1.anode, C6.0
  N16: Anemômetro.pin_2, C6.1
  N17: R4.Pin_0, C5.0, D5.anode
  N18: V1.V+, S1.leg0
  N19: C4.0, R7.Pin_0, D4.anode
  N20: D2.anode, R6.Pin_1, R7.Pin_1, Pluviômetro.pin_1, C7.0
  N21: Pluviômetro.pin_2, C7.1

custom parts:
  Adafruit_BMP280: Bosch has stepped up their game with their new BMP280 sensor, an environmental sensor with temperature, barometric pressure that is the next generation upgrade to the BMP085/BMP180/BMP183. This sensor is great for all sorts of weather sensing and can even be used in both I2C and SPI! This precision sensor from Bosch is the best low-cost, precision sensing solution for measuring barometric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
