# Fritzing sketch Esquema elétrico sistema IT - v4 - RTC - protoboard - Com manutenção (saved by Fritzing 0.9.3b)
perfboards: 1

parts:
  J5 = female pin header, 8 pins [form="♀ (female)"]
  J6 = female pin header, 8 pins [form="♀ (female)"]
  WeMos_D1_Mini1 = WeMos D1 Mini  # not connected
  U1 = attiny85 [package=dip]
  R1 = Resistor [tolerance=±5% resistance=330 package=THT]
  C2 = Electrolytic Capacitor [capacitance=4.7mF package="100 mil [THT, electrolytic]"]  # not connected
  R2 = Resistor [tolerance=±5% resistance=330 package=THT]
  R3 = Resistor [tolerance=±5% resistance=1k package=THT]
  R4 = Resistor [tolerance=±5% resistance=1k package=THT]
  D2 = Rectifier Diode [part_number=1N4001 package="300 mil [THT]"]
  C3 = Ceramic Capacitor [capacitance=100nF package="100 mil [THT, multilayer]"]
  D4 = Rectifier Diode [part_number=1N4001 package="300 mil [THT]"]
  C5 = Ceramic Capacitor [capacitance=100nF package="100 mil [THT, multilayer]"]
  R5 = Resistor [tolerance=±5% resistance=220 package=THT]  # not connected
  J9 = female pin header, 7 pins [form="♀ (female)"]
  J4 = female pin header, 9 pins [form="♀ (female)"]
  J3 = female pin header, 9 pins [form="♀ (female)"]
  C6 = Electrolytic Capacitor [capacitance=4.7mF package="100 mil [THT, electrolytic]"]  # not connected
  R6 = Resistor [tolerance=±5% resistance=47k package=THT]
  R7 = Resistor [tolerance=±5% resistance=10k package=THT]
  J2 = female pin header, 9 pins [form="♀ (female)"]
  J1 = female pin header, 9 pins [form="♀ (female)"]
  J11 = female pin header, 5 pins [form="♀ (female)"]
  J7 = female pin header, 6 pins [form="♀ (female)"]
  D1 = Rectifier Diode [part_number=1N4001 package="300 mil [THT]"]
  D5 = Rectifier Diode [part_number=1N4001 package="300 mil [THT]"]
  C7 = Ceramic Capacitor [capacitance=100nF package="100 mil [THT, multilayer]"]  # not connected
  C8 = Ceramic Capacitor [capacitance=100nF package="100 mil [THT, multilayer]"]
  C9 = Ceramic Capacitor [capacitance=100nF package="100 mil [THT, multilayer]"]
  J13 = male pin header, 3 pins [form="♂ (male)"]
  S1 = Toggle Switch [package=THT]
  J16 = male pin header, 2 pins [form="♂ (male)"]
  J17 = male pin header, 2 pins [form="♂ (male)"]  # not connected
  D6 = Rectifier Diode [part_number=1N4001 package="300 mil [THT]"]
  D7 = Rectifier Diode [part_number=1N4001 package="300 mil [THT]"]
  D8 = Rectifier Diode [part_number=1N4001 package="300 mil [THT]"]
  R8 = Resistor [tolerance=±5% resistance=10k package=THT]
  LED1 = LED - 3mm [color="Red (633nm)" package="3 mm [THT]"]
  R9 = Resistor [tolerance=±5% resistance=330 package=THT]
  R10 = Resistor [tolerance=±5% resistance=82 package=THT]
  J12 = male pin header, 2 pins [form="♂ (male)"]
  J10 = male pin header, 2 pins [form="♂ (male)"]

nets:
  N1: J5.pin1, J9.pin4, J7.pin6
  N2: J5.pin2, J9.pin1
  N3: J5.pin3, J9.pin2
  N4: J5.pin5, J9.pin5
  N5: J5.pin6, J10.pin2
  N6: J5.pin8, J10.pin1
  N7: J6.pin1, S1.COM
  N8: J6.pin2, J7.pin5
  N9: J6.pin4, J13.pin3
  N10: J6.pin5, J1.pin2, J11.pin2, J7.pin3
  N11: J6.pin6, J1.pin4, J11.pin3, J7.pin4
  N12: J6.pin7, J16.pin2
  N13: J6.pin8, J3.pin8
  N14: U1.Pin_2, J3.pin4, R6.Pin_1
  N15: U1.Pin_3, J13.pin1
  N16: U1.Pin_5, D6.cathode
  N17: U1.Pin_6, R1.Pin_1, D2.cathode, C3.0
  N18: U1.Pin_7, R2.Pin_1, D4.cathode, C8.0
  N19: R1.Pin_0, R4.Pin_0, D2.anode, J2.pin2
  N20: R2.Pin_0, R3.Pin_1, D4.anode
  N21: R3.Pin_0, D1.anode, C8.1
  N22: R4.Pin_1, C3.1, D5.anode
  N23: C5.0, J2.pin6
  N24: J4.pin4, R10.Pin_0
  N25: J4.pin8, R6.Pin_0, C9.1, S1.L2
  N26: J3.pin2, R7.Pin_0
  N27: J3.pin6, D7.cathode
  N28: R7.Pin_1, C9.0
  N29: J16.pin1, D6.anode, D7.anode, D8.anode
  N30: D8.cathode, J12.pin2
  N31: R8.Pin_1, R9.Pin_1
  N32: LED1.anode, R9.Pin_0

notes:
  (x) Jumper para interromper barramento RX serial do ESP8266
  (x) jumper no pino attiny que recebe sinal de solicitação de serial vindo do esp*
  (x) jumper entre RST e D0 para reset
  * vai a trilha até próximo so attiny, e lá coloco um pino para encaixar e fechar o circuito
  BMP 280 [4 pin std header]
  SD [7 pin]
  SD
  RST Jumper
  RTC ->
  Serial Jumper
