# Fritzing sketch Esquema elétrico auxiliar para exemplo de protoboard - rev3 (saved by Fritzing 0.9.3b)
perfboards: 1

parts:
  J5 = female pin header, 8 pins [form="♀ (female)"]
  J6 = female pin header, 8 pins [form="♀ (female)"]
  WeMos_D1_Mini1 = WeMos D1 Mini  # not connected
  U1 = attiny85 [package=dip]
  R1 = Resistor [tolerance=±5% resistance=330 package=THT]
  C2 = Electrolytic Capacitor [capacitance=0.47mF voltage=16V package="100 mil [THT, electrolytic]"]  # not connected
  R2 = Resistor [tolerance=±5% resistance=330 package=THT]
  R3 = Resistor [tolerance=±5% resistance=1k package=THT]
  R4 = Resistor [tolerance=±5% resistance=1k package=THT]
  D2 = Rectifier Diode [part_number=1N4001 package="300 mil [THT]"]
  C3 = Ceramic Capacitor [capacitance=100nF package="100 mil [THT, multilayer]"]
  D4 = Rectifier Diode [part_number=1N4001 package="300 mil [THT]"]
  C5 = Ceramic Capacitor [capacitance=100nF package="100 mil [THT, multilayer]"]
  R5 = Resistor [tolerance=±5% resistance=220 package=THT]
  J9 = female pin header, 7 pins [form="♀ (female)"]
  C6 = Electrolytic Capacitor [capacitance=0.47mF voltage=16V package="100 mil [THT, electrolytic]"]
  R6 = Resistor [tolerance=±5% resistance=47k package=THT]
  R7 = Resistor [tolerance=±5% resistance=10k package=THT]
  J11 = female pin header, 5 pins [form="♀ (female)"]
  D1 = Rectifier Diode [part_number=1N4001 package="300 mil [THT]"]
  D5 = Rectifier Diode [part_number=1N4001 package="300 mil [THT]"]
  C7 = Ceramic Capacitor [capacitance=100nF package="100 mil [THT, multilayer]"]  # not connected
  C8 = Ceramic Capacitor [capacitance=100nF package="100 mil [THT, multilayer]"]
  C9 = Ceramic Capacitor [capacitance=100nF package="100 mil [THT, multilayer]"]
  J16 = male pin header, 2 pins [form="♂ (male)"]
  J17 = male pin header, 2 pins [form="♂ (male)"]  # not connected
  J10 = male pin header, 2 pins [form="♂ (male)"]
  J12 = male pin header, 2 pins [form="♂ (male)"]
  J13 = male pin header, 2 pins [form="♂ (male)"]
  J7 = female pin header, 4 pins [form="♀ (female)"]
  J18 = male pin header, 2 pins [form="♂ (male)"]
  J19 = male pin header, 1 pin [form="♂ (male)"]
  J21 = male pin header, 1 pin [form="♂ (male)"]
  J22 = male pin header, 1 pin [form="♂ (male)"]  # not connected
  J23 = male pin header, 1 pin [form="♂ (male)"]  # not connected
  J24 = male pin header, 1 pin [form="♂ (male)"]
  J25 = male pin header, 1 pin [form="♂ (male)"]  # not connected
  J26 = male pin header, 1 pin [form="♂ (male)"]
  J27 = male pin header, 1 pin [form="♂ (male)"]
  J28 = male pin header, 1 pin [form="♂ (male)"]
  J29 = male pin header, 1 pin [form="♂ (male)"]
  J30 = male pin header, 1 pin [form="♂ (male)"]
  J31 = male pin header, 1 pin [form="♂ (male)"]  # not connected
  J32 = male pin header, 1 pin [form="♂ (male)"]
  J33 = male pin header, 1 pin [form="♂ (male)"]  # not connected
  J34 = male pin header, 1 pin [form="♂ (male)"]  # not connected
  J35 = male pin header, 1 pin [form="♂ (male)"]
  R9 = Resistor [tolerance=±5% resistance=10k package=THT]
  R10 = Resistor [tolerance=±5% resistance=82 package=THT]
  D6 = Rectifier Diode [part_number=1N4001 package="300 mil [THT]"]
  LED1 = LED - 3mm [color="Red (633nm)" package="3 mm [THT]"]
  D7 = Rectifier Diode [part_number=1N4001 package="300 mil [THT]"]
  D9 = Rectifier Diode [part_number=1N4001 package="300 mil [THT]"]
  R11 = Resistor [tolerance=±5% resistance=330 package=THT]

nets:
  N1: J5.pin1, J9.pin4, J7.pin4
  N2: J5.pin2, J9.pin1
  N3: J5.pin3, J9.pin2
  N4: J5.pin4, R5.Pin_0, J9.pin7
  N5: J5.pin5, J9.pin5
  N6: J5.pin6, J10.pin2
  N7: J5.pin8, J10.pin1
  N8: J6.pin1, J18.pin1
  N9: J6.pin2, J7.pin3
  N10: J6.pin4, J13.pin2
  N11: J6.pin5, J11.pin2, J7.pin1, J19.pin1
  N12: J6.pin6, J11.pin3, J7.pin2, J21.pin1
  N13: J6.pin7, J12.pin1
  N14: J6.pin8, J30.pin1
  N15: U1.Pin_2, R6.Pin_1, J28.pin1
  N16: U1.Pin_3, J13.pin1
  N17: U1.Pin_5, D6.cathode
  N18: U1.Pin_6, R1.Pin_1, D2.cathode, C3.0
  N19: U1.Pin_7, R2.Pin_1, D4.cathode, C8.0
  N20: R1.Pin_0, R4.Pin_0, D2.anode, J24.pin1
  N21: R2.Pin_0, R3.Pin_1, D4.anode
  N22: R3.Pin_0, D1.anode, C8.1
  N23: R4.Pin_1, C3.1, D5.anode
  N24: C5.0, J26.pin1
  N25: C6.+, R10.Pin_1, R11.Pin_1
  N26: R6.Pin_0, C9.1, J18.pin2, J32.pin1
  N27: R7.Pin_0, J27.pin1
  N28: R7.Pin_1, C9.0
  N29: J16.pin1, D7.cathode
  N30: J12.pin2, R9.Pin_0
  N31: J29.pin1, D9.cathode
  N32: J35.pin1, R10.Pin_0
  N33: D6.anode, D7.anode
  N34: LED1.anode, R11.Pin_0

notes:
  SD [7 pin]
  SD
  Reset (J1) ->
  RTC ->
  Serial (J2) ->
  SHT20 - SCL ->
  Anemômetro* ->
  Sensor de Direção do Vento*  ->
  Serial RX ->
  5V input ->
  î Pin 3 (J3)
  Serial Pins ->
  Pinos 5V, GND ->
  Jumper/chave
  SHT20 - SDA ->
  SHT20 - GND ->
  SHT20 - 3.3V ->
  Pluviômetro* ->
  Serial TX ->
  GND ->
  Conexões/Bornes:
  *Com asterisco são conexões sem polaridade.
  GND¹ ->
  3.3V output¹ ->
  ¹ Borne conectado ao barramento de energia
  GND e 3.3V (max 40mA).
  <- BMP280 - SCL
  <- BMP280 - SDA
  <- BMP280 - 3.3V
  <- BMP280 - GND
  ESQUEMA AUXILIAR PARA MONTAGEM/MANUTENÇÃO
  Pinos de depuração e monitoramento:
  - Serial Pins -> o branco é RX e o cinza é TX do sistema;
  -Pinos 5V, GND -> permite monitorar a tensão de 5v do sistema.
  Para atualizar firmware do ESP8266 remova:
  - Jumper J1, entre RST e D0 (reset/deepsleep);
  - Jumper J2, interrompendo barramento RX serial;
  - Jumper J3, pino 3 do ATtiny85 que recebe sinal de solicitação de serial vindo do esp8266;
  - Jumper (ou desligue a chave) de liga-desliga do sistema.
  Em seguida conecte o cabo na porta micro USB do ESP8266.
  J3: Pin 3 jumper
  J2: Serial RX jumper
  J1: Reset (RST) jumper
  Liga-Desliga
