# Fritzing sketch Esquema elétrico estação meteorológica - rev3 (saved by Fritzing 0.9.3b)
breadboards: 1

parts:
  DIP8 = attiny85 [package=dip]
  ESP8266 = WeMos D1 Mini
  Direção_do_Vento = Trimmer Potentiometer [maximum_resistance=80kΩ package=THT]
  Anemômetro = Reed switch [package=THT]
  Barômetro = Adafruit_BMP280
  Micro_SD = MicroSD Card Module
  SHT20 = Humidity Temperature Sensor SHT15
  R3 = Resistor [tolerance=±5% resistance=10k package=THT]
  R4 = Resistor [tolerance=±5% resistance=1k package=THT]
  R5 = Resistor [tolerance=±5% resistance=330 package=THT]
  D1 = Rectifier Diode [part_number=1N4001 package="Melf DO-213 AB [SMD]"]
  V1 = DC Power [voltage=5V]
  C4 = Ceramic Capacitor [capacitance=100nF package="100 mil [THT, multilayer]"]
  D2 = Rectifier Diode [part_number=1N4001 package="Melf DO-213 AB [SMD]"]
  R6 = Resistor [tolerance=±5% resistance=330 package=THT]
  R7 = Resistor [tolerance=±5% resistance=1k package=THT]
  C5 = Ceramic Capacitor [capacitance=100nF package="100 mil [THT, multilayer]"]
  Pluviômetro = Reed switch [package=THT]
  R10 = Resistor [tolerance=±5% resistance=220 package=THT]
  C6 = Ceramic Capacitor [capacitance=100nF package="100 mil [THT, multilayer]"]
  C7 = Ceramic Capacitor [capacitance=100nF package="100 mil [THT, multilayer]"]
  RTC1 = RTC Module
  D4 = Rectifier Diode [part_number=1N4001 package="Melf DO-213 AB [SMD]"]
  D5 = Rectifier Diode [part_number=1N4001 package="Melf DO-213 AB [SMD]"]
  R11 = Resistor [tolerance=±5% resistance=47k package=THT]
  C8 = Ceramic Capacitor [capacitance=100nF package="100 mil [THT, multilayer]"]
  C9 = Electrolytic Capacitor [capacitance=0.47mF package="100 mil [THT, electrolytic]"]
  C10 = Electrolytic Capacitor [capacitance=0.47mF package="100 mil [THT, electrolytic]"]
  S1 = Pushbutton [package=THT]
  J2 = Jumper [package=sj_2s-no]
  J3 = Jumper [package=sj_2s-no]
  Pins_(5V_GND) = female pin header, 2 pins [form="♀ (female)"]
  J1 = Jumper [package=sj_2s-no]
  Bornes_(3_3V_max_40mA_GND) = female pin header, 2 pins [form="♀ (female)"]
  R12 = Resistor [tolerance=±5% resistance=10k package=THT]
  R13 = Resistor [tolerance=±5% resistance=330 package=THT]
  R14 = Resistor [tolerance=±5% resistance=82 package=THT]
  D8 = Rectifier Diode [part_number=1N4001 package="300 mil [THT]"]
  D9 = Rectifier Diode [part_number=1N4001 package="300 mil [THT]"]
  LED1 = LED - 5mm [color="Red (633nm)" package="5 mm [THT]"]
  Serial_Com = female pin header, 4 pins [form="♀ (female)"]
  D10 = Rectifier Diode [part_number=1N4001 package="300 mil [THT]"]

nets:
  N1: DIP8.Pin_2, Direção_do_Vento.leg2, R11.Pin_1
  N2: DIP8.Pin_3, J3.2
  GND: DIP8.Pin_4, ESP8266.G, Barômetro.GND, Micro_SD.GND, SHT20.GND, R3.Pin_0, V1.V-, D4.cathode, D5.cathode, C8.1, C9.-, C10.-, Pins_(5V_GND).pin2, Bornes_(3_3V_max_40mA_GND).pin2, LED1.cathode
  N3: DIP8.Pin_5, D10.cathode
  N4: DIP8.Pin_6, C4.1, D2.cathode, R6.Pin_0
  N5: DIP8.Pin_7, R5.Pin_0, D1.cathode, C5.1
  VCC: DIP8.Pin_8, ESP8266.3V3, Barômetro.3.3V, Micro_SD.VCC, SHT20.VCC, R10.Pin_1, RTC1.VCC, C10.+, R12.Pin_0, R13.Pin_1, R14.Pin_0
  N6: ESP8266.5V, R11.Pin_0, C8.0, S1.leg1
  N7: ESP8266.D0, J1.1
  N8: ESP8266.D1, Barômetro.SCK/SCL, SHT20.SCL, RTC1.SCL
  N9: ESP8266.D2, Barômetro.SDI/SDA, SHT20.SDA, RTC1.SDA
  N10: ESP8266.D3, J3.1
  N11: ESP8266.D5, Micro_SD.SCK
  N12: ESP8266.D6, Micro_SD.MISO, R10.Pin_0
  N13: ESP8266.D7, Micro_SD.MOSI
  N14: ESP8266.D8, Micro_SD.CS
  N15: ESP8266.RST, J1.2
  N16: ESP8266.RX, J2.2
  N17: ESP8266.TX, Serial_Com.pin2, Serial_Com.pin4
  N18: Direção_do_Vento.wiper, R3.Pin_1
  N19: Anemômetro.pin_1, R4.Pin_1, R5.Pin_1, D1.anode, C6.0
  N20: Anemômetro.pin_2, C6.1
  N21: R4.Pin_0, C5.0, D5.anode
  N22: V1.V+, C9.+, S1.leg0, Pins_(5V_GND).pin1
  N23: C4.0, R7.Pin_0, D4.anode
  N24: D2.anode, R6.Pin_1, R7.Pin_1, Pluviômetro.pin_1, C7.0
  N25: Pluviômetro.pin_2, C7.1
  N26: J2.1, R12.Pin_1, D8.anode, D9.anode, D10.anode
  N27: Bornes_(3_3V_max_40mA_GND).pin1, R14.Pin_1
  N28: R13.Pin_0, LED1.anode
  N29: D8.cathode, Serial_Com.pin1
  N30: D9.cathode, Serial_Com.pin3

notes:
  J1: Reset (RST) jumper
  J2: Serial RX jumper
  J3: Pin 3 jumper
  ESQUEMA ELÉTRICO

custom parts:
  Adafruit_BMP280: Bosch has stepped up their game with their new BMP280 sensor, an environmental sensor with temperature, barometric pressure that is the next generation upgrade to the BMP085/BMP180/BMP183. This sensor is great for all sorts of weather sensing and can even be used in both I2C and SPI! This precision sensor from Bosch is the best low-cost, precision sensing solution for measuring barometric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
